// Logisim project 8_Bit.circ as structural Verilog: 4 circuits, main circuit HalfAdder
module HalfAdder (
  input  Input_A,
  input  Input_B,
  output Sum,
  output Carry
);

  xor xor_1 (Sum, Input_A, Input_B);
  and and_1 (Carry, Input_A, Input_B);
endmodule

module FullAdder (
  input  Carry_In,
  input  Input_A,
  input  Input_B,
  output Carry_Out,
  output Sum
);

  wire halfadder_1_carry, halfadder_2_carry, halfadder_2_sum;

  HalfAdder halfadder_1 (.Input_A(Carry_In), .Input_B(halfadder_2_sum), .Sum(Sum), .Carry(halfadder_1_carry));
  HalfAdder halfadder_2 (.Input_A(Input_A), .Input_B(Input_B), .Sum(halfadder_2_sum), .Carry(halfadder_2_carry));
  or or_1 (Carry_Out, halfadder_1_carry, halfadder_2_carry);
endmodule

module main (
  input  A1,
  input  B1,
  input  A2,
  input  B2,
  input  A3,
  input  B3,
  input  A4,
  input  B4,
  input  A5,
  input  B5,
  input  A6,
  input  B6,
  input  A7,
  input  B7,
  input  A8,
  input  B8,
  output C1,
  output C2,
  output C3,
  output C4,
  output C5,
  output C6,
  output C7,
  output C8
);

  wire fulladder_1_carry_out, fulladder_2_carry_out, fulladder_3_carry_out, fulladder_4_carry_out,
       fulladder_5_carry_out, fulladder_6_carry_out, fulladder_7_carry_out, fulladder_8_carry_out;

  FullAdder fulladder_1 (.Carry_In(1'b0), .Input_A(B1), .Input_B(A1), .Carry_Out(fulladder_1_carry_out), .Sum(C1));
  FullAdder fulladder_2 (
    .Carry_In(fulladder_1_carry_out), .Input_A(B2), .Input_B(A2), .Carry_Out(fulladder_2_carry_out), .Sum(C2));
  FullAdder fulladder_3 (
    .Carry_In(fulladder_2_carry_out), .Input_A(B3), .Input_B(A3), .Carry_Out(fulladder_3_carry_out), .Sum(C3));
  FullAdder fulladder_4 (
    .Carry_In(fulladder_3_carry_out), .Input_A(B4), .Input_B(A4), .Carry_Out(fulladder_4_carry_out), .Sum(C4));
  FullAdder fulladder_5 (
    .Carry_In(fulladder_4_carry_out), .Input_A(B5), .Input_B(A5), .Carry_Out(fulladder_5_carry_out), .Sum(C5));
  FullAdder fulladder_6 (
    .Carry_In(fulladder_5_carry_out), .Input_A(B6), .Input_B(A6), .Carry_Out(fulladder_6_carry_out), .Sum(C6));
  FullAdder fulladder_7 (
    .Carry_In(fulladder_6_carry_out), .Input_A(B7), .Input_B(A7), .Carry_Out(fulladder_7_carry_out), .Sum(C7));
  LED Overflow (.in(fulladder_8_carry_out));
  FullAdder fulladder_8 (
    .Carry_In(fulladder_7_carry_out), .Input_A(B8), .Input_B(A8), .Carry_Out(fulladder_8_carry_out), .Sum(C8));
endmodule

module EBAdder (
  input  [7:0] in_1,
  output [7:0] out_2
);

  main main_1 (
    .A1(in_1[0]), .A2(in_1[1]), .A3(in_1[2]), .A4(in_1[3]), .A5(in_1[4]), .A6(in_1[5]), .A7(in_1[6]),
    .A8(in_1[7]));  // open: B1, B2, B3, B4, B5, B6, B7, B8, C1, C2, C3, C4, C5, C6, C7, C8
endmodule
